# Fritzing sketch videojoystick (saved by Fritzing 0.9.5d)
breadboards: 1

parts:
  U1 = ESP32S-HiLetgo [part_number=ESP32S-HiLetgo]
  Part1 = Thumb Joystick
  Part2 = Thumb Joystick
  U2 = Voltage Regulator - 5V [package="TO220 [THT]"]
  C1 = Capacitor [package=cap-pth-small2]
  C2 = Capacitor [package=cap-pth-small2]
  VCC1 = Battery block 9V
  S1 = Toggle Switch [package=THT]
  R1 = Resistor [tolerance=±5% resistance=220 package="1206 [SMD]"]
  R2 = Resistor [tolerance=±5% resistance=220 package="1206 [SMD]"]
  OLED1 = WaveShare 1.3 inch OLED

nets:
  VCC: U1.3.3, Part1.VCC, Part2.VCC, R1.Pin_1, R2.Pin_1, OLED1.VCC
  N1: U1.GPIO36, Part1.HORZ
  N2: U1.GPIO39, Part1.SEL
  N3: U1.GPIO34, Part1.GND
  N4: U1.GPIO35, Part2.HORZ
  N5: U1.GPIO32, Part2.SEL
  N6: U1.GPIO25, S1.L1, R1.Pin_0
  N7: U1.GPIO26, S1.L2, R2.Pin_0
  GND: U1.GND, Part1.VERT, Part2.VERT, U2.GND, C1.2, C2.1, VCC1.-, S1.COM, OLED1.GND
  N8: U1.GPIO13, Part2.GND
  N9: U1.VIN, U2.input_voltage, C2.2
  N10: U1.GPIO0, OLED1.RES
  N11: U1.GPIO4, OLED1.D/C
  N12: U1.GPIO5, OLED1.CS
  N13: U1.GPIO18, OLED1.CLK
  N14: U1.GPIO23, OLED1.DIN
  N15: U2.output_voltage, C1.1, VCC1.+

custom parts:
  ESP32S-HiLetgo: HiLetgo ESP-WROOM-32 ESP32 ESP-32S Development Board 2.4GHz Dual-Mode WiFi + Bluetooth Dual Cores Microcontroller The ESP32 integrated with Antenna switches, RF Balun, power amplifiers, low-noise amplifiers, filters, and management modules, and the entire solution occupies the least area of PCB. 2.4 GHz Wi-Fi plus Bluetooth dual-mode chip, with TSMC Ultra-low power consumption 40nm technology,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
  WaveShare 1.3 inch OLED: 128x64 Monochrom OLED Display with a SH1106 controller
